# Fritzing sketch sh_arduino (saved by Fritzing 0.9.4)
circuit board: 8cm x 6cm
stripboards: 1

parts:
  Часть7 = Arduino Nano (Rev3.0)
  C1 = Ceramic Capacitor [capacitance=0.1mF voltage=0.1kV package="100 mil [THT, multilayer]"]
  LED2 = LED - 5mm [color="Red (633nm)" package="5 mm [THT]"]
  R8 = Resistor [tolerance=±5% resistance=47k package=THT]
  Q7 = NPN-Transistor [part_number=PN2222 package="TO92 [THT]"]
  R9 = Resistor [tolerance=±5% resistance=680 package=THT]
  R10 = Resistor [tolerance=±5% resistance=1k package=THT]
  Q9 = npn-Powertransistor [package="TO220 [THT]"]
  D1 = Rectifier Diode [part_number=1N4001 package="300 mil [THT]"]
  J6_Arduino-Fan = male pin header, 2 pins [form="♂ (male)" part_number="12V, GND"]
  J7_Arduino-Button = male pin header, 2 pins [form="♂ (male)"]
  J5_Arduino_Downstep5V = male pin header, 1 pin [form="♂ (male)"]
  J4_Arduino-RPi = male pin header, 4 pins [form="♂ (male)" part_number="5V, GND, GPIO4, PEN"]
  J1_Arduino-INA226 = male pin header, 4 pins [form="♂ (male)" part_number="12V, GND, SDA, SCL"]
  J3_Arduino-Downstep3V = male pin header, 1 pin [form="♂ (male)" part_number=3V3]
  J2_Arduino-Sensors = male pin header, 4 pins [form="♂ (male)" part_number="3V3, GND, SDA, SCL"]

nets:
  N1: Часть7.GND, C1.0, Q7.E, Q9.emitter, J7_Arduino-Button.pin1, J4_Arduino-RPi.pin2, J1_Arduino-INA226.pin2, J2_Arduino-Sensors.pin2
  N2: Часть7.D3, R10.Pin_1
  N3: Часть7.D6, J7_Arduino-Button.pin2
  N4: Часть7.D8, LED2.anode
  N5: Часть7.D9, R8.Pin_1
  N6: Часть7.VIN, C1.1, D1.cathode, J6_Arduino-Fan.pin1, J1_Arduino-INA226.pin1
  N7: Часть7.A5, J1_Arduino-INA226.pin4, J2_Arduino-Sensors.pin4
  N8: Часть7.A4, J1_Arduino-INA226.pin3, J2_Arduino-Sensors.pin3
  N9: LED2.cathode, J4_Arduino-RPi.pin3
  N10: R8.Pin_0, Q7.B
  N11: Q7.C, R9.Pin_1
  N12: R9.Pin_0, J4_Arduino-RPi.pin4
  N13: R10.Pin_0, Q9.base
  N14: Q9.collector, D1.anode, J6_Arduino-Fan.pin2
  N15: J5_Arduino_Downstep5V.pin1, J4_Arduino-RPi.pin1
  N16: J3_Arduino-Downstep3V.pin1, J2_Arduino-Sensors.pin1
